// Logisim project Modulo-10 U-D Counter.circ as structural Verilog: 1 circuit, main circuit main
module main (
  input  UP_DOWN,
  output [3:0] OUTPUT
);

  wire and_1_out, and_2_out, and_3_out, and_4_out, and_5_out, and_6_out, and_7_out, and_8_out, and_9_out,
       and_10_out, and_11_out, CLEAR_out, CLOCK_out, JK1_qn, JK2_qn, JK3_qn, JK4_qn, multiplexer_1_out,
       multiplexer_2_out, multiplexer_3_out, or_1_out, or_2_out, or_3_out;

  Button CLEAR (.out(CLEAR_out));
  Clock CLOCK (.out(CLOCK_out));
  J_K_Flip_Flop JK1 (
    .J(1'b1), .clk(CLOCK_out), .K(1'b1), .Q(OUTPUT[0]), .Qn(JK1_qn), .reset(CLEAR_out));  // open: preset, en
  and and_1 (and_1_out, OUTPUT[0], JK4_qn);
  and and_2 (and_2_out, OUTPUT[1], JK1_qn);
  and and_3 (and_3_out, OUTPUT[2], JK1_qn);
  and and_4 (and_4_out, OUTPUT[3], JK1_qn);
  Multiplexer #(.enable("false")) multiplexer_1 (
    .in0(and_1_out), .in1(or_1_out), .out(multiplexer_1_out), .sel(UP_DOWN));
  or or_1 (or_1_out, and_2_out, and_3_out, and_4_out);
  J_K_Flip_Flop JK2 (
    .J(multiplexer_1_out), .clk(CLOCK_out), .K(multiplexer_1_out), .Q(OUTPUT[1]), .Qn(JK2_qn),
    .reset(CLEAR_out));  // open: preset, en
  and and_5 (and_5_out, OUTPUT[0], OUTPUT[1]);
  and and_6 (and_6_out, JK2_qn, JK1_qn);
  and and_7 (and_7_out, OUTPUT[2], and_6_out);
  and and_8 (and_8_out, and_6_out, OUTPUT[3]);
  Multiplexer #(.enable("false")) multiplexer_2 (
    .in0(and_5_out), .in1(or_2_out), .out(multiplexer_2_out), .sel(UP_DOWN));
  or or_2 (or_2_out, and_7_out, and_8_out);
  J_K_Flip_Flop JK3 (
    .J(multiplexer_2_out), .clk(CLOCK_out), .K(multiplexer_2_out), .Q(OUTPUT[2]), .Qn(JK3_qn),
    .reset(CLEAR_out));  // open: preset, en
  and and_9 (and_9_out, and_5_out, OUTPUT[2]);
  and and_10 (and_10_out, OUTPUT[0], OUTPUT[3]);
  or or_3 (or_3_out, and_9_out, and_10_out);
  Multiplexer #(.enable("false")) multiplexer_3 (
    .in0(or_3_out), .in1(and_11_out), .out(multiplexer_3_out), .sel(UP_DOWN));
  and and_11 (and_11_out, JK3_qn, JK2_qn, JK1_qn);
  Hex_Digit_Display hex_digit_display_1 (.value(OUTPUT));  // open: dp
  J_K_Flip_Flop JK4 (
    .J(multiplexer_3_out), .clk(CLOCK_out), .K(multiplexer_3_out), .Q(OUTPUT[3]), .Qn(JK4_qn),
    .reset(CLEAR_out));  // open: preset, en
endmodule
