// Logisim project Seven Segment LED.circ as structural Verilog: 3 circuits, main circuit Counter
// 7 Segment Decoder
module main (
  input  UP_DOWN
);

  wire _7_Segment_a, _7_Segment_b, _7_Segment_c, _7_Segment_d, _7_Segment_e, _7_Segment_f, _7_Segment_g,
       CLEAR_out, CLOCK_out;
  wire [3:0] COUNTER_output;

  Clock CLOCK (.out(CLOCK_out));
  Counter COUNTER (.CLOCK(CLOCK_out), .Up_Down(UP_DOWN), .CLEAR(CLEAR_out), .OUTPUT(COUNTER_output));
  Button CLEAR (.out(CLEAR_out));
  _7_Segment _7_Segment (
    .b3(COUNTER_output[3]), .b2(COUNTER_output[2]), .b1(COUNTER_output[1]), .b0(COUNTER_output[0]),
    .a(_7_Segment_a), .b(_7_Segment_b), .c(_7_Segment_c), .d(_7_Segment_d), .e(_7_Segment_e),
    .f(_7_Segment_f), .g(_7_Segment_g));
  _7_Segment_Display u_7_segment_display_1 (
    .g(_7_Segment_g), .f(_7_Segment_f), .a(_7_Segment_a), .b(_7_Segment_b), .e(_7_Segment_e),
    .d(_7_Segment_d), .c(_7_Segment_c));  // open: dp

  // Notes on the sheet:
  //   7-Segment Display
endmodule

module _7_Segment (
  input  b3,
  input  b2,
  input  b1,
  input  b0,
  output a,
  output b,
  output c,
  output d,
  output e,
  output f,
  output g
);

  wire and_1_out, and_2_out, and_3_out, and_4_out, and_5_out, and_6_out, and_7_out, and_8_out, and_9_out,
       and_10_out, and_11_out, and_12_out, and_13_out, and_14_out, and_15_out, and_16_out, and_17_out,
       and_18_out, and_19_out, and_20_out, and_21_out, and_22_out, and_23_out, and_24_out, and_25_out,
       and_26_out, not_1_out, not_2_out, not_3_out, not_4_out, not_5_out, not_6_out, not_7_out, not_8_out,
       not_9_out, not_10_out, not_11_out, not_12_out, not_13_out, not_14_out, not_15_out, not_16_out,
       not_17_out, not_18_out, not_19_out, not_20_out, not_21_out, not_22_out, not_23_out, not_24_out,
       not_25_out, not_26_out, not_27_out, not_28_out, not_29_out, not_30_out, not_31_out, not_32_out,
       not_33_out, not_34_out, not_35_out, not_36_out, not_37_out, not_38_out, not_39_out, not_40_out,
       not_41_out, not_42_out, not_43_out, not_44_out, not_45_out, not_46_out, not_47_out, not_48_out,
       not_49_out, not_50_out, not_51_out, not_52_out;

  not not_1 (not_1_out, b3);
  and and_1 (and_1_out, not_1_out, not_2_out, not_3_out);
  not not_2 (not_2_out, b2);
  not not_3 (not_3_out, b0);
  not not_4 (not_4_out, b3);
  and and_2 (and_2_out, not_4_out, b1);
  not not_5 (not_5_out, b3);
  and and_3 (and_3_out, not_5_out, b2, b0);
  and and_4 (and_4_out, b3, not_6_out, not_7_out);
  not not_6 (not_6_out, b2);
  not not_7 (not_7_out, b1);
  not not_8 (not_8_out, b3);
  and and_5 (and_5_out, not_8_out, not_9_out);
  not not_9 (not_9_out, b2);
  not not_10 (not_10_out, b3);
  not not_11 (not_11_out, b1);
  and and_6 (and_6_out, not_10_out, not_11_out, not_12_out);
  not not_12 (not_12_out, b0);
  not not_13 (not_13_out, b2);
  and and_7 (and_7_out, not_13_out, not_14_out);
  not not_14 (not_14_out, b1);
  not not_15 (not_15_out, b3);
  and and_8 (and_8_out, not_15_out, b1, b0);
  not not_16 (not_16_out, b2);
  and and_9 (and_9_out, not_16_out, not_17_out);
  not not_17 (not_17_out, b1);
  not not_18 (not_18_out, b3);
  and and_10 (and_10_out, not_18_out, b0);
  not not_19 (not_19_out, b3);
  and and_11 (and_11_out, not_19_out, b2);
  not not_20 (not_20_out, b3);
  not not_21 (not_21_out, b2);
  not not_22 (not_22_out, b0);
  not not_23 (not_23_out, b3);
  not not_24 (not_24_out, b2);
  not not_25 (not_25_out, b3);
  not not_26 (not_26_out, b0);
  not not_27 (not_27_out, b3);
  not not_28 (not_28_out, b1);
  not not_29 (not_29_out, b2);
  not not_30 (not_30_out, b1);
  not not_31 (not_31_out, b2);
  and and_12 (and_12_out, not_31_out, not_32_out, not_33_out);
  not not_32 (not_32_out, b1);
  not not_33 (not_33_out, b0);
  not not_34 (not_34_out, b3);
  and and_13 (and_13_out, not_34_out, b1, not_35_out);
  not not_35 (not_35_out, b0);
  not not_36 (not_36_out, b3);
  not not_37 (not_37_out, b1);
  and and_14 (and_14_out, not_36_out, not_37_out, not_38_out);
  not not_38 (not_38_out, b0);
  not not_39 (not_39_out, b3);
  and and_15 (and_15_out, not_39_out, b2, not_40_out);
  not not_40 (not_40_out, b1);
  not not_41 (not_41_out, b3);
  and and_16 (and_16_out, not_41_out, b2, not_42_out);
  not not_42 (not_42_out, b0);
  not not_43 (not_43_out, b2);
  and and_17 (and_17_out, b3, not_43_out, not_44_out);
  not not_44 (not_44_out, b1);
  not not_45 (not_45_out, b3);
  not not_46 (not_46_out, b2);
  and and_18 (and_18_out, not_45_out, not_46_out, b1);
  not not_47 (not_47_out, b3);
  and and_19 (and_19_out, not_47_out, b2, not_48_out);
  not not_48 (not_48_out, b1);
  not not_49 (not_49_out, b3);
  and and_20 (and_20_out, not_49_out, b2, not_50_out);
  not not_50 (not_50_out, b0);
  and and_21 (and_21_out, b3, not_51_out, not_52_out);
  not not_51 (not_51_out, b2);
  not not_52 (not_52_out, b1);
  or or_1 (a, and_1_out, and_2_out, and_3_out, and_4_out);
  or or_2 (b, and_5_out, and_6_out, and_7_out, and_8_out);
  or or_3 (c, and_9_out, and_10_out, and_11_out);
  and and_22 (and_22_out, not_20_out, not_21_out, not_22_out);
  and and_23 (and_23_out, not_23_out, not_24_out, b1);
  and and_24 (and_24_out, not_25_out, b1, not_26_out);
  and and_25 (and_25_out, not_27_out, b2, not_28_out, b0);
  and and_26 (and_26_out, b3, not_29_out, not_30_out);
  or or_4 (e, and_12_out, and_13_out);
  or or_5 (f, and_14_out, and_15_out, and_16_out, and_17_out);
  or or_6 (g, and_18_out, and_19_out, and_20_out, and_21_out);
  or or_7 (d, and_22_out, and_23_out, and_24_out, and_25_out, and_26_out);
endmodule

module Counter (
  input  CLOCK,
  input  Up_Down,
  input  CLEAR,
  output [3:0] OUTPUT
);

  wire and_1_out, and_2_out, and_3_out, and_4_out, and_5_out, and_6_out, and_7_out, and_8_out, and_9_out,
       and_10_out, and_11_out, JK1_qn, JK2_qn, JK3_qn, JK4_qn, multiplexer_1_out, multiplexer_2_out,
       multiplexer_3_out, or_1_out, or_2_out, or_3_out;

  J_K_Flip_Flop JK1 (.J(1'b1), .clk(CLOCK), .K(1'b1), .Q(OUTPUT[0]), .Qn(JK1_qn), .reset(CLEAR));  // open: preset, en
  and and_1 (and_1_out, OUTPUT[0], JK4_qn);
  and and_2 (and_2_out, OUTPUT[1], JK1_qn);
  and and_3 (and_3_out, OUTPUT[2], JK1_qn);
  and and_4 (and_4_out, OUTPUT[3], JK1_qn);
  Multiplexer #(.enable("false")) multiplexer_1 (
    .in0(and_1_out), .in1(or_1_out), .out(multiplexer_1_out), .sel(Up_Down));
  or or_1 (or_1_out, and_2_out, and_3_out, and_4_out);
  J_K_Flip_Flop JK2 (
    .J(multiplexer_1_out), .clk(CLOCK), .K(multiplexer_1_out), .Q(OUTPUT[1]), .Qn(JK2_qn), .reset(CLEAR));  // open: preset, en
  and and_5 (and_5_out, OUTPUT[0], OUTPUT[1]);
  and and_6 (and_6_out, JK2_qn, JK1_qn);
  and and_7 (and_7_out, OUTPUT[2], and_6_out);
  and and_8 (and_8_out, and_6_out, OUTPUT[3]);
  Multiplexer #(.enable("false")) multiplexer_2 (
    .in0(and_5_out), .in1(or_2_out), .out(multiplexer_2_out), .sel(Up_Down));
  or or_2 (or_2_out, and_7_out, and_8_out);
  J_K_Flip_Flop JK3 (
    .J(multiplexer_2_out), .clk(CLOCK), .K(multiplexer_2_out), .Q(OUTPUT[2]), .Qn(JK3_qn), .reset(CLEAR));  // open: preset, en
  and and_9 (and_9_out, and_5_out, OUTPUT[2]);
  and and_10 (and_10_out, OUTPUT[0], OUTPUT[3]);
  or or_3 (or_3_out, and_9_out, and_10_out);
  Multiplexer #(.enable("false")) multiplexer_3 (
    .in0(or_3_out), .in1(and_11_out), .out(multiplexer_3_out), .sel(Up_Down));
  and and_11 (and_11_out, JK3_qn, JK2_qn, JK1_qn);
  J_K_Flip_Flop JK4 (
    .J(multiplexer_3_out), .clk(CLOCK), .K(multiplexer_3_out), .Q(OUTPUT[3]), .Qn(JK4_qn), .reset(CLEAR));  // open: preset, en

  // Notes on the sheet:
  //   U/D Mod-10 Counter
endmodule
