// Logisim project Cascaded Mod-60 Counter.circ as structural Verilog: 3 circuits, main circuit Mod-10 Counter
module Cascade__0_59 (
  input  UP_DOWN
);

  wire and_1_out, and_2_out, CLEAR_out, CLOCK_out, multiplexer_1_out, not_1_out, not_2_out, not_3_out,
       not_4_out, not_5_out, not_6_out;
  wire [2:0] Mod_6_Counter_output;
  wire [3:0] Mod_10_Counter_output;

  Button CLEAR (.out(CLEAR_out));
  not not_1 (not_1_out, Mod_10_Counter_output[1]);
  Clock CLOCK (.out(CLOCK_out));
  not not_2 (not_2_out, Mod_10_Counter_output[0]);
  not not_3 (not_3_out, Mod_10_Counter_output[2]);
  not not_4 (not_4_out, Mod_10_Counter_output[1]);
  not not_5 (not_5_out, Mod_10_Counter_output[2]);
  and and_1 (and_1_out, not_2_out, not_1_out, not_3_out, not_6_out);
  not not_6 (not_6_out, Mod_10_Counter_output[3]);
  and and_2 (and_2_out, Mod_10_Counter_output[0], not_4_out, not_5_out, Mod_10_Counter_output[3]);
  Mod_10_Counter Mod_10_Counter (.CLK(CLOCK_out), .S(UP_DOWN), .CLEAR(CLEAR_out), .OUTPUT(Mod_10_Counter_output));
  Mod_6_Counter Mod_6_Counter (.CLK(multiplexer_1_out), .S(UP_DOWN), .CLEAR(CLEAR_out), .OUTPUT(Mod_6_Counter_output));
  Hex_Digit_Display hex_digit_display_1 (.value({1'b0, Mod_6_Counter_output}));  // open: dp
  Multiplexer #(.enable("false")) multiplexer_1 (
    .in0(and_1_out), .in1(and_2_out), .out(multiplexer_1_out), .sel(UP_DOWN));
  Hex_Digit_Display hex_digit_display_2 (.value(Mod_10_Counter_output));  // open: dp

  // Notes on the sheet:
  //   Cascaded Mod-60 Counter
endmodule

module Mod_10_Counter (
  input  CLK,
  input  S,
  input  CLEAR,
  output [3:0] OUTPUT
);

  wire and_1_out, and_2_out, and_3_out, and_4_out, and_5_out, and_6_out, and_7_out, and_8_out, and_9_out,
       and_10_out, and_11_out, JK1_qn, JK2_qn, JK3_qn, JK4_qn, multiplexer_1_out, multiplexer_2_out,
       multiplexer_3_out, or_1_out, or_2_out, or_3_out;

  J_K_Flip_Flop JK1 (.J(1'b1), .clk(CLK), .K(1'b1), .Q(OUTPUT[0]), .Qn(JK1_qn), .reset(CLEAR));  // open: preset, en
  and and_1 (and_1_out, OUTPUT[0], JK4_qn);
  and and_2 (and_2_out, OUTPUT[1], JK1_qn);
  and and_3 (and_3_out, OUTPUT[2], JK1_qn);
  and and_4 (and_4_out, OUTPUT[3], JK1_qn);
  Multiplexer #(.enable("false")) multiplexer_1 (.in0(and_1_out), .in1(or_1_out), .out(multiplexer_1_out), .sel(S));
  or or_1 (or_1_out, and_2_out, and_3_out, and_4_out);
  J_K_Flip_Flop JK2 (
    .J(multiplexer_1_out), .clk(CLK), .K(multiplexer_1_out), .Q(OUTPUT[1]), .Qn(JK2_qn), .reset(CLEAR));  // open: preset, en
  and and_5 (and_5_out, OUTPUT[0], OUTPUT[1]);
  and and_6 (and_6_out, JK2_qn, JK1_qn);
  and and_7 (and_7_out, OUTPUT[2], and_6_out);
  and and_8 (and_8_out, and_6_out, OUTPUT[3]);
  Multiplexer #(.enable("false")) multiplexer_2 (.in0(and_5_out), .in1(or_2_out), .out(multiplexer_2_out), .sel(S));
  or or_2 (or_2_out, and_7_out, and_8_out);
  J_K_Flip_Flop JK3 (
    .J(multiplexer_2_out), .clk(CLK), .K(multiplexer_2_out), .Q(OUTPUT[2]), .Qn(JK3_qn), .reset(CLEAR));  // open: preset, en
  and and_9 (and_9_out, and_5_out, OUTPUT[2]);
  and and_10 (and_10_out, OUTPUT[0], OUTPUT[3]);
  or or_3 (or_3_out, and_9_out, and_10_out);
  Multiplexer #(.enable("false")) multiplexer_3 (.in0(or_3_out), .in1(and_11_out), .out(multiplexer_3_out), .sel(S));
  and and_11 (and_11_out, JK3_qn, JK2_qn, JK1_qn);
  J_K_Flip_Flop JK4 (
    .J(multiplexer_3_out), .clk(CLK), .K(multiplexer_3_out), .Q(OUTPUT[3]), .Qn(JK4_qn), .reset(CLEAR));  // open: preset, en

  // Notes on the sheet:
  //   U/D Mod-10 Counter
endmodule

module Mod_6_Counter (
  input  CLK,
  input  S,
  input  CLEAR,
  output [2:0] OUTPUT
);

  wire and_1_out, and_2_out, and_3_out, and_4_out, and_5_out, and_6_out, JK1_qn, JK2_qn, JK3_qn,
       multiplexer_1_out, multiplexer_2_out, or_1_out, or_2_out;

  J_K_Flip_Flop JK1 (.J(1'b1), .clk(CLK), .K(1'b1), .Q(OUTPUT[0]), .Qn(JK1_qn), .reset(CLEAR));  // open: preset, en
  and and_1 (and_1_out, JK3_qn, OUTPUT[0]);
  and and_2 (and_2_out, OUTPUT[2], JK1_qn);
  or or_1 (or_1_out, and_2_out, and_3_out);
  and and_3 (and_3_out, JK1_qn, OUTPUT[1]);
  Multiplexer multiplexer_1 (.in0(and_1_out), .in1(or_1_out), .out(multiplexer_1_out), .sel(S));  // open: en
  J_K_Flip_Flop JK2 (
    .J(multiplexer_1_out), .clk(CLK), .K(multiplexer_1_out), .Q(OUTPUT[1]), .Qn(JK2_qn), .reset(CLEAR));  // open: preset, en
  and and_4 (and_4_out, OUTPUT[2], OUTPUT[0]);
  and and_5 (and_5_out, OUTPUT[0], OUTPUT[1]);
  or or_2 (or_2_out, and_4_out, and_5_out);
  and and_6 (and_6_out, JK2_qn, JK1_qn);
  Multiplexer multiplexer_2 (.in0(or_2_out), .in1(and_6_out), .out(multiplexer_2_out), .sel(S));  // open: en
  J_K_Flip_Flop JK3 (
    .J(multiplexer_2_out), .clk(CLK), .K(multiplexer_2_out), .Q(OUTPUT[2]), .Qn(JK3_qn), .reset(CLEAR));  // open: preset, en

  // Notes on the sheet:
  //   U/D Mod-6 Counter
endmodule
