// Logisim project Traffic Signal System.circ as structural Verilog: 9 circuits, main circuit Mod 10 Counter
module Main_Circuit (
  input  BUSY_SELECTOR,
  input  CLEAR,
  input  ON_OFF
);

  wire CLOCK_out, Control_Circuit_g, Control_Circuit_g_2, Control_Circuit_g_3, Control_Circuit_g_4,
       Control_Circuit_r, Control_Circuit_r_2, Control_Circuit_r_3, Control_Circuit_r_4, Control_Circuit_y,
       Control_Circuit_y_2, Control_Circuit_y_3, Control_Circuit_y_4;
  wire [3:0] Control_Circuit_ten, Control_Circuit_unit;

  LED led_1 (.in(Control_Circuit_r_3));
  LED led_2 (.in(Control_Circuit_y_3));
  LED led_3 (.in(Control_Circuit_g_3));
  LED led_4 (.in(Control_Circuit_r_2));
  LED led_5 (.in(Control_Circuit_y_2));
  LED led_6 (.in(Control_Circuit_g_2));
  Control_Circuit Control_Circuit (
    .BUSY(BUSY_SELECTOR), .ON_OFF(ON_OFF), .G_2(Control_Circuit_g_2), .Y_2(Control_Circuit_y_2),
    .R_2(Control_Circuit_r_2), .G_3(Control_Circuit_g_3), .Y_3(Control_Circuit_y_3),
    .R_3(Control_Circuit_r_3), .R_4(Control_Circuit_r_4), .G_4(Control_Circuit_g_4),
    .Y_4(Control_Circuit_y_4), .R(Control_Circuit_r), .Y(Control_Circuit_y), .G(Control_Circuit_g),
    .CLEAR(CLEAR), .CLOCK(CLOCK_out), .TEN(Control_Circuit_ten), .UNIT(Control_Circuit_unit));
  LED led_7 (.in(Control_Circuit_r_4));
  LED led_8 (.in(Control_Circuit_y_4));
  LED led_9 (.in(Control_Circuit_g_4));
  Clock CLOCK (.out(CLOCK_out));
  LED led_10 (.in(Control_Circuit_r));
  LED led_11 (.in(Control_Circuit_y));
  LED led_12 (.in(Control_Circuit_g));
  Hex_Digit_Display hex_digit_display_1 (.value(Control_Circuit_ten));  // open: dp
  Hex_Digit_Display hex_digit_display_2 (.value(Control_Circuit_unit));  // open: dp

  // Notes on the sheet:
  //   0 = Off
  //   [
  //   1 = On
  //   W
  //   ]
  //   >
  //   N
  //   ^
  //   S
  //   V
  //   Traffic Signal System
  //   <
  //   E
endmodule

module Control_Circuit (
  input  CLEAR,
  input  CLOCK,
  input  BUSY,
  input  ON_OFF,
  output [3:0] TEN,
  output [3:0] UNIT,
  output R,
  output Y,
  output G,
  output G_2,
  output Y_2,
  output R_2,
  output G_3,
  output Y_3,
  output R_3,
  output R_4,
  output G_4,
  output Y_4
);

  wire [2:0] Signal_Count_output;
  wire [3:0] Signal_Count_ten_1, Signal_Count_ten_2, Signal_Count_unit_1, Signal_Count_unit_2;

  or or_1 (R_2, Y_3, G_3, Y, G, Y_4, G_4);
  or or_2 (R_3, Y, G, Y_4, G_4, Y_2, G_2);
  Signal_Count Signal_Count (
    .CLOCK_0(CLOCK), .CLEAR(CLEAR), .CLOCK_1(CLOCK), .Ten_1(Signal_Count_ten_1), .Ten_2(Signal_Count_ten_2),
    .Unit_1(Signal_Count_unit_1), .Unit_2(Signal_Count_unit_2), .OUTPUT(Signal_Count_output),
    .BUSY_SELECTOR(BUSY));  // open: CLEAR_COUNTER
  Decoder #(.select(3)) decoder_1 (
    .out0(G_2), .out1(Y_2), .out2(G_4), .out3(Y_4), .out4(G), .out5(Y), .out6(G_3), .out7(Y_3),
    .sel(Signal_Count_output), .en(ON_OFF));
  Multiplexer #(.width(4), .enable("false")) multiplexer_1 (
    .in0(Signal_Count_ten_1), .in1(Signal_Count_ten_2), .out(TEN), .sel(BUSY));
  Multiplexer #(.width(4), .enable("false")) multiplexer_2 (
    .in0(Signal_Count_unit_1), .in1(Signal_Count_unit_2), .out(UNIT), .sel(BUSY));
  or or_3 (R_4, Y_2, G_2, G, Y, G_3, Y_3);
  Hex_Digit_Display hex_digit_display_1 (.value(UNIT));  // open: dp
  Hex_Digit_Display hex_digit_display_2 (.value(TEN));  // open: dp
  or or_4 (R, Y_3, G_3, Y_4, G_4, Y_2, G_2);

  // Notes on the sheet:
  //   S
  //   W
  //   Cntrol Circuit
  //   N
  //   E
endmodule

module Signal_Count (
  input  CLOCK_0,
  input  CLEAR_COUNTER,
  input  CLEAR,
  input  BUSY_SELECTOR,
  input  CLOCK_1,
  output [3:0] Ten_1,
  output [3:0] Unit_1,
  output [2:0] OUTPUT,
  output [3:0] Ten_2,
  output [3:0] Unit_2
);

  wire and_1_out, and_2_out, and_3_out, and_4_out, and_5_out, and_6_out, and_7_out, and_8_out, and_9_out,
       and_10_out, multiplexer_1_out, not_1_out, not_2_out, not_3_out, not_4_out, not_5_out, not_6_out,
       not_7_out, not_8_out, not_9_out, not_10_out, not_11_out, not_12_out, not_13_out, not_14_out,
       not_15_out, or_1_out, or_2_out;

  Mod_30_Counter Mod_30_Counter (.Clock(CLOCK_0), .Clear(CLEAR), .Output_1(Ten_1), .Output_0(Unit_1));
  Mod_60_Counter Mod_60_Counter (.Clock(CLOCK_1), .Clear(CLEAR), .Output_1(Ten_2), .Output_0(Unit_2));
  not not_1 (not_1_out, Ten_2[1]);
  not not_2 (not_2_out, Unit_1[1]);
  and and_1 (and_1_out, Unit_1[0], not_2_out, not_3_out, Unit_1[3]);
  not not_3 (not_3_out, Unit_1[2]);
  not not_4 (not_4_out, Ten_1[0]);
  and and_2 (and_2_out, not_4_out, Ten_1[1], not_5_out, not_6_out);
  not not_5 (not_5_out, Ten_1[2]);
  not not_6 (not_6_out, Ten_1[3]);
  not not_7 (not_7_out, Ten_1[1]);
  and and_3 (and_3_out, Ten_1[0], not_7_out, not_8_out, not_9_out);
  not not_8 (not_8_out, Ten_1[2]);
  not not_9 (not_9_out, Ten_1[3]);
  not not_10 (not_10_out, Unit_2[1]);
  and and_4 (and_4_out, Unit_2[0], not_10_out, not_11_out, Unit_2[3]);
  not not_11 (not_11_out, Unit_2[2]);
  and and_5 (and_5_out, Ten_2[0], not_1_out, Ten_2[2], not_12_out);
  not not_12 (not_12_out, Ten_2[3]);
  not not_13 (not_13_out, Ten_2[0]);
  not not_14 (not_14_out, Ten_2[1]);
  and and_6 (and_6_out, not_13_out, not_14_out, Ten_2[2], not_15_out);
  not not_15 (not_15_out, Ten_2[3]);
  Hex_Digit_Display hex_digit_display_1 (.value(Ten_1));  // open: dp
  Hex_Digit_Display hex_digit_display_2 (.value(Ten_2));  // open: dp
  Hex_Digit_Display hex_digit_display_3 (.value(Unit_1));  // open: dp
  and and_7 (and_7_out, and_1_out, and_2_out);
  and and_8 (and_8_out, and_1_out, and_3_out);
  Hex_Digit_Display hex_digit_display_4 (.value(Unit_2));  // open: dp
  and and_9 (and_9_out, and_4_out, and_5_out);
  and and_10 (and_10_out, and_4_out, and_6_out);
  or or_1 (or_1_out, and_7_out, and_8_out);
  or or_2 (or_2_out, and_9_out, and_10_out);
  Multiplexer #(.enable("false")) multiplexer_1 (
    .in0(or_1_out), .in1(or_2_out), .out(multiplexer_1_out), .sel(BUSY_SELECTOR));
  Counter #(.width(3), .max('h7)) Mod_8_Counter (
    .Q(OUTPUT), .clk(multiplexer_1_out), .clr(CLEAR_COUNTER));  // open: load, D, count, carry

  // Notes on the sheet:
  //   SIgnal Count
endmodule

module Mod_60_Counter (
  input  Clock,
  input  Clear,
  output [3:0] Output_1,
  output [3:0] Output_0
);

  wire Logic_Circuit_output;

  Mod_10_Counter Mod_10_Counter (.Clock(Clock), .Clear(Clear), .Output(Output_0));
  Logic_Circuit Logic_Circuit (.Input(Output_0), .Output(Logic_Circuit_output));
  Mod_6_Counter MOD_6_Counter (.Clock(Logic_Circuit_output), .Clear(Clear), .Output(Output_1));

  // Notes on the sheet:
  //   MOD-60 Counter
endmodule

module Mod_30_Counter (
  input  Clock,
  input  Clear,
  output [3:0] Output_1,
  output [3:0] Output_0
);

  wire Logic_Circuit_output;

  Mod_10_Counter Mod_10_Counter (.Clock(Clock), .Clear(Clear), .Output(Output_0));
  Logic_Circuit Logic_Circuit (.Input(Output_0), .Output(Logic_Circuit_output));
  Mod_3_Counter Mod_3_Counter (.Clock(Logic_Circuit_output), .Clear(Clear), .Output(Output_1));

  // Notes on the sheet:
  //   MOD-30 Counter
endmodule

module Mod_10_Counter (
  input  Clock,
  input  Clear,
  output [3:0] Output
);

  wire and_1_out, and_2_out, and_3_out, and_4_out, j_k_ff_4_qn, or_1_out;

  and and_1 (and_1_out, Output[0], j_k_ff_4_qn);
  J_K_Flip_Flop j_k_ff_1 (.J(1'b1), .clk(Clock), .K(1'b1), .Q(Output[0]), .reset(Clear));  // open: Qn, preset, en
  J_K_Flip_Flop j_k_ff_2 (
    .J(and_1_out), .clk(Clock), .K(and_1_out), .Q(Output[1]), .reset(Clear));  // open: Qn, preset, en
  and and_2 (and_2_out, Output[0], Output[1]);
  J_K_Flip_Flop j_k_ff_3 (
    .J(and_2_out), .clk(Clock), .K(and_2_out), .Q(Output[2]), .reset(Clear));  // open: Qn, preset, en
  and and_3 (and_3_out, and_2_out, Output[2]);
  or or_1 (or_1_out, and_3_out, and_4_out);
  and and_4 (and_4_out, Output[0], Output[3]);
  J_K_Flip_Flop j_k_ff_4 (
    .J(or_1_out), .clk(Clock), .K(or_1_out), .Q(Output[3]), .Qn(j_k_ff_4_qn), .reset(Clear));  // open: preset, en

  // Notes on the sheet:
  //   Mod 10 Counter
endmodule

module Mod_6_Counter (
  input  Clock,
  input  Clear,
  output [3:0] Output
);

  wire and_1_out, and_2_out, and_3_out, j_k_ff_3_qn, or_1_out;

  J_K_Flip_Flop j_k_ff_1 (.J(1'b1), .clk(Clock), .K(1'b1), .Q(Output[0]), .reset(Clear));  // open: Qn, preset, en
  J_K_Flip_Flop j_k_ff_2 (
    .J(and_1_out), .clk(Clock), .K(and_1_out), .Q(Output[1]), .reset(Clear));  // open: Qn, preset, en
  and and_1 (and_1_out, j_k_ff_3_qn, Output[0]);
  and and_2 (and_2_out, Output[2], Output[0]);
  and and_3 (and_3_out, Output[0], Output[1]);
  or or_1 (or_1_out, and_2_out, and_3_out);
  J_K_Flip_Flop j_k_ff_3 (
    .J(or_1_out), .clk(Clock), .K(or_1_out), .Q(Output[2]), .Qn(j_k_ff_3_qn), .reset(Clear));  // open: preset, en

  assign Output[3] = 1'b0;

  // Notes on the sheet:
  //   MOD-6 Counter
endmodule

module Mod_3_Counter (
  input  Clock,
  input  Clear,
  output [3:0] Output
);

  wire j_k_ff_1_qn;

  J_K_Flip_Flop j_k_ff_1 (
    .J(Output[0]), .clk(Clock), .K(1'b1), .Q(Output[1]), .Qn(j_k_ff_1_qn), .reset(Clear));  // open: preset, en
  J_K_Flip_Flop j_k_ff_2 (
    .J(j_k_ff_1_qn), .clk(Clock), .K(1'b1), .Q(Output[0]), .reset(Clear));  // open: Qn, preset, en

  assign Output[3:2] = 2'b00;

  // Notes on the sheet:
  //   MOD-3 Counter
endmodule

module Logic_Circuit (
  input  [3:0] Input,
  output Output
);

  wire not_1_out, not_2_out, not_3_out, not_4_out;

  not not_1 (not_1_out, Input[1]);
  not not_2 (not_2_out, Input[3]);
  not not_3 (not_3_out, Input[0]);
  not not_4 (not_4_out, Input[2]);
  and and_1 (Output, not_3_out, not_1_out, not_4_out, not_2_out);

  // Notes on the sheet:
  //   Logic Circuit
endmodule
