// Logisim project 3-BIT-ADDER-W-REGISTER.circ as structural Verilog: 7 circuits, main circuit main
module main (
  input  in_1,
  input  in_2,
  output [2:0] out_3,
  output [2:0] out_4,
  output [2:0] out_5,
  output CARRY
);

  wire clock_1_out;
  wire [2:0] counter_1_out_3, counter_2_out_3;

  Clock clock_1 (.out(clock_1_out));
  COUNTER counter_1 (.CLOCK(clock_1_out), .RESET(in_1), .out_3(counter_1_out_3));
  COUNTER counter_2 (.CLOCK(clock_1_out), .RESET(in_2), .out_3(counter_2_out_3));
  REGISTER register_1 (.in_1(clock_1_out), .in_2(counter_1_out_3), .out_3(out_3));
  REGISTER register_2 (.in_1(clock_1_out), .in_2(counter_2_out_3), .out_3(out_4));
  _3_bit_ADDER u_3_bit_adder_1 (.in_1(out_3), .in_2(out_4), .out_3(out_5), .out_4(CARRY));
endmodule

module COUNTER (
  input  CLOCK,
  input  RESET,
  output [2:0] out_3
);

  wire t_ff_1_q, t_ff_2_q;

  T_Flip_Flop t_ff_1 (.clk(CLOCK), .T(1'b1), .Q(t_ff_1_q), .Qn(out_3[0]), .reset(RESET));  // open: preset, en
  T_Flip_Flop t_ff_2 (.clk(t_ff_1_q), .T(1'b1), .Q(t_ff_2_q), .Qn(out_3[1]), .reset(RESET));  // open: preset, en
  T_Flip_Flop t_ff_3 (.clk(t_ff_2_q), .T(1'b1), .Qn(out_3[2]), .reset(RESET));  // open: Q, preset, en
endmodule

module REGISTER (
  input  in_1,
  input  [2:0] in_2,
  output [2:0] out_3
);

  D_Flip_Flop d_ff_1 (.clk(in_1), .D(in_2[0]), .Q(out_3[0]));  // open: Qn, preset, en, reset
  D_Flip_Flop d_ff_2 (.clk(in_1), .D(in_2[1]), .Q(out_3[1]));  // open: Qn, preset, en, reset
  D_Flip_Flop d_ff_3 (.clk(in_1), .D(in_2[2]), .Q(out_3[2]));  // open: Qn, preset, en, reset
endmodule

module OR (
  input  in_1,
  input  in_2,
  output out_3
);

  wire nand_1_out, nand_2_out;

  nand nand_1 (nand_1_out, in_1, in_1);
  nand nand_2 (nand_2_out, in_2, in_2);
  nand nand_3 (out_3, nand_1_out, nand_2_out);
endmodule

module HALF_ADDER (
  input  A,
  input  B,
  output Sum,
  output Carry
);

  wire nand_1_out, nand_2_out, nand_4_out;

  nand nand_1 (nand_1_out, A, B);
  nand nand_2 (nand_2_out, A, nand_1_out);
  nand nand_3 (Sum, nand_2_out, nand_4_out);
  nand nand_4 (nand_4_out, nand_1_out, B);
  nand nand_5 (Carry, nand_1_out, nand_1_out);
endmodule

module FULL_ADDER (
  input  A,
  input  B,
  input  Cin,
  output out_4,
  output out_5
);

  wire half_adder_1_carry, half_adder_1_sum, half_adder_2_carry;

  HALF_ADDER half_adder_1 (.A(A), .B(B), .Sum(half_adder_1_sum), .Carry(half_adder_1_carry));
  HALF_ADDER half_adder_2 (.A(half_adder_1_sum), .B(Cin), .Sum(out_5), .Carry(half_adder_2_carry));
  OR or_1 (.in_1(half_adder_2_carry), .in_2(half_adder_1_carry), .out_3(out_4));
endmodule

module _3_bit_ADDER (
  input  [2:0] in_1,
  input  [2:0] in_2,
  output [2:0] out_3,
  output out_4
);

  wire full_adder_1_out_4, half_adder_1_carry;

  HALF_ADDER half_adder_1 (.A(in_1[0]), .B(in_2[0]), .Sum(out_3[0]), .Carry(half_adder_1_carry));
  FULL_ADDER full_adder_1 (
    .A(in_1[1]), .B(in_2[1]), .Cin(half_adder_1_carry), .out_4(full_adder_1_out_4), .out_5(out_3[1]));
  FULL_ADDER full_adder_2 (.A(in_1[2]), .B(in_2[2]), .Cin(full_adder_1_out_4), .out_4(out_4), .out_5(out_3[2]));
endmodule
