// Logisim project 3-BIT-ADDER.circ as structural Verilog: 1 circuit, main circuit main
module main (
  input  A1,
  input  A0,
  input  B1,
  input  B0,
  output O2,
  output O1,
  output O0
);

  wire nand_1_out, nand_2_out, nand_3_out, nand_5_out, nand_6_out, nand_7_out, nand_8_out, nand_9_out,
       nand_10_out, nand_12_out, nand_13_out;

  nand nand_1 (nand_1_out, A0, B0);
  nand nand_2 (nand_2_out, nand_1_out, nand_1_out);
  nand nand_3 (nand_3_out, A0, nand_1_out);
  nand nand_4 (O0, nand_3_out, nand_5_out);
  nand nand_5 (nand_5_out, nand_1_out, B0);
  nand nand_6 (nand_6_out, A1, B1);
  nand nand_7 (nand_7_out, A1, nand_6_out);
  nand nand_8 (nand_8_out, nand_7_out, nand_9_out);
  nand nand_9 (nand_9_out, nand_6_out, B1);
  nand nand_10 (nand_10_out, nand_8_out, nand_2_out);
  nand nand_11 (O2, nand_6_out, nand_10_out);
  nand nand_12 (nand_12_out, nand_8_out, nand_10_out);
  nand nand_13 (nand_13_out, nand_10_out, nand_2_out);
  nand nand_14 (O1, nand_12_out, nand_13_out);
endmodule
