// Logisim project 3-BIT-SERIAL-ADDER.circ as structural Verilog: 7 circuits, main circuit main
module main (
  input  PI,
  input  SI,
  input  A2,
  input  A1,
  input  A0,
  input  B2,
  input  B1,
  input  B0,
  output A2_2,
  output A1_2,
  output A0_2,
  output B2_2,
  output B1_2,
  output B0_2
);

  wire clock_1_out, d_ff_1_q, full_adder_1_carry, full_adder_1_sum;

  Clock clock_1 (.out(clock_1_out));
  Shift_Register_PI_SO shift_register_pi_so_1 (
    .CLOCK(clock_1_out), .OUT_2(A2_2), .OUT_1(A1_2), .OUT_0(A0_2), .PI(PI), .SI(SI), .I1(A2),
    .O1(full_adder_1_sum), .I2(A1), .I3(A0));
  Shift_Register_PI_SO shift_register_pi_so_2 (
    .CLOCK(clock_1_out), .OUT_2(B2_2), .OUT_1(B1_2), .OUT_0(B0_2), .PI(PI), .SI(SI), .I1(B2), .I2(B1), .I3(B0));  // open: O1
  FULL_ADDER full_adder_1 (.A(A0_2), .B(B0_2), .C(d_ff_1_q), .SUM(full_adder_1_sum), .CARRY(full_adder_1_carry));
  D_Flip_Flop d_ff_1 (.clk(clock_1_out), .D(full_adder_1_carry), .Q(d_ff_1_q));  // open: Qn, preset, en, reset
endmodule

// SHIFT-REG
module Shift_Register_PI_SO (
  input  CLOCK,
  input  I1,
  input  O1,
  input  I2,
  input  I3,
  input  PI,
  input  SI,
  output OUT_2,
  output OUT_1,
  output OUT_0
);

  wire and_1_out_3, and_2_out_3, and_3_out_3, and_4_out_3, and_5_out_3, and_6_out_3, or_1_out_3, or_2_out_3,
       or_3_out_3;

  OR or_1 (.A(and_1_out_3), .B(and_2_out_3), .out_3(or_1_out_3));
  AND and_1 (.A(I1), .B(PI), .out_3(and_1_out_3));
  AND and_2 (.A(SI), .B(O1), .out_3(and_2_out_3));
  D_Flip_Flop d_ff_1 (.clk(CLOCK), .D(or_1_out_3), .Q(OUT_2));  // open: Qn, preset, en, reset
  OR or_2 (.A(and_3_out_3), .B(and_4_out_3), .out_3(or_2_out_3));
  AND and_3 (.A(OUT_2), .B(SI), .out_3(and_3_out_3));
  AND and_4 (.A(PI), .B(I2), .out_3(and_4_out_3));
  D_Flip_Flop d_ff_2 (.clk(CLOCK), .D(or_2_out_3), .Q(OUT_1));  // open: Qn, preset, en, reset
  OR or_3 (.A(and_5_out_3), .B(and_6_out_3), .out_3(or_3_out_3));
  AND and_5 (.A(OUT_1), .B(SI), .out_3(and_5_out_3));
  AND and_6 (.A(PI), .B(I3), .out_3(and_6_out_3));
  D_Flip_Flop d_ff_3 (.clk(CLOCK), .D(or_3_out_3), .Q(OUT_0));  // open: Qn, preset, en, reset
endmodule

module AND (
  input  A,
  input  B,
  output out_3
);

  wire nand_1_out;

  nand nand_1 (nand_1_out, A, B);
  nand nand_2 (out_3, nand_1_out, nand_1_out);
endmodule

module OR (
  input  A,
  input  B,
  output out_3
);

  wire not_1_out_2, not_2_out_2;

  NOT not_1 (.A(A), .out_2(not_1_out_2));
  NOT not_2 (.A(B), .out_2(not_2_out_2));
  nand nand_1 (out_3, not_1_out_2, not_2_out_2);
endmodule

module NOT (
  input  A,
  output out_2
);

  nand nand_1 (out_2, A, A);
endmodule

module X_OR (
  input  A,
  input  B,
  output out_3
);

  wire nand_1_out, nand_2_out, nand_3_out;

  nand nand_1 (nand_1_out, A, B);
  nand nand_2 (nand_2_out, A, nand_1_out);
  nand nand_3 (nand_3_out, nand_1_out, B);
  nand nand_4 (out_3, nand_2_out, nand_3_out);
endmodule

// ADD
module FULL_ADDER (
  input  A,
  input  B,
  input  C,
  output SUM,
  output CARRY
);

  wire and_1_out_3, and_2_out_3, x_or_1_out_3;

  X_OR x_or_1 (.A(A), .B(B), .out_3(x_or_1_out_3));
  AND and_1 (.A(A), .B(B), .out_3(and_1_out_3));
  X_OR x_or_2 (.A(x_or_1_out_3), .B(C), .out_3(SUM));
  AND and_2 (.A(C), .B(x_or_1_out_3), .out_3(and_2_out_3));
  OR or_1 (.A(and_2_out_3), .B(and_1_out_3), .out_3(CARRY));
endmodule
