// Logisim project BCD-To-Excess-3.circ as structural Verilog: 1 circuit, main circuit main
module main (
  input  A,
  input  [2:0] B_C_D,
  input  in_3,
  input  in_4,
  output G3,
  output G2,
  output G1,
  output G0
);

  Multiplexer #(.select(3)) multiplexer_1 (
    .in0(A), .in1(A), .in2(A), .in3(A), .in4(A), .in5(in_4), .in6(in_4), .in7(in_4), .out(G3), .sel(B_C_D),
    .en(in_4));
  Multiplexer #(.select(3)) multiplexer_2 (
    .in0(in_3), .in1(in_4), .in2(in_4), .in3(in_4), .in4(in_4), .in5(A), .in6(A), .in7(A), .out(G2),
    .sel(B_C_D), .en(in_4));
  Multiplexer #(.select(3)) multiplexer_3 (
    .in0(in_4), .in1(in_3), .in2(A), .in3(in_4), .in4(in_4), .in5(A), .in6(A), .in7(in_4), .out(G1),
    .sel(B_C_D), .en(in_4));
  Multiplexer #(.select(3)) multiplexer_4 (
    .in0(in_4), .in1(in_3), .in2(in_4), .in3(A), .in4(in_4), .in5(A), .in6(in_4), .in7(A), .out(G0),
    .sel(B_C_D), .en(in_4));
endmodule
