// Logisim project GRAY.circ as structural Verilog: 2 circuits, main circuit main
module main (
  input  b2,
  input  b1,
  input  b0,
  output g2,
  output g1,
  output g0
);

  XOR xor_1 (.P(b2), .Q(b1), .R(g1));
  XOR xor_2 (.P(b1), .Q(b0), .R(g0));

  assign g2 = b2;
endmodule

module XOR (
  input  P,
  input  Q,
  output R
);

  wire nand_1_out, nand_2_out, nand_3_out;

  nand nand_1 (nand_1_out, P, Q);
  nand nand_2 (nand_2_out, P, nand_1_out);
  nand nand_3 (nand_3_out, nand_1_out, Q);
  nand nand_4 (R, nand_2_out, nand_3_out);
endmodule
