// Logisim project HomeWork.circ as structural Verilog: 9 circuits, main circuit main
module main (
  input  Subtractor,
  input  [3:0] A,
  input  [3:0] B,
  input  Enable,
  output [3:0] A_O,
  output [3:0] B_2,
  output Carry
);

  wire Add_out, Adder_c, clock_1_out, multiplexer_3_out, nand_1_out, nand_2_out;
  wire [3:0] Adder_s, multiplexer_1_out, multiplexer_2_out;

  Button Add (.out(Add_out));
  nand nand_1 (nand_1_out, nand_2_out, nand_2_out);
  nand nand_2 (nand_2_out, Add_out, Add_out);
  Multiplexer #(.width(4), .enable("false")) multiplexer_1 (
    .in0(Adder_s), .in1(A), .out(multiplexer_1_out), .sel(nand_2_out));
  Multiplexer #(.width(4), .enable("false")) multiplexer_2 (
    .in0(B), .in1(4'b0000), .out(multiplexer_2_out), .sel(nand_1_out));
  _4_bit_register Register (.in_2(clock_1_out), .in_3(Enable), .in_1(multiplexer_2_out), .out_4(B_2));
  _4_bit_register Register_2 (.in_2(clock_1_out), .in_3(Enable), .in_1(multiplexer_1_out), .out_4(A_O));
  _4_bit_parallel_adder Adder (.A(A_O), .B(B_2), .C(Adder_c), .in_3(Subtractor), .S(Adder_s));
  Multiplexer #(.enable("false")) multiplexer_3 (.in0(Carry), .in1(Adder_c), .out(multiplexer_3_out), .sel(nand_2_out));
  D_flipflop D_flip (.in_2(multiplexer_3_out), .out_4(Carry), .in_3(Enable), .in_1(clock_1_out));
  Clock clock_1 (.out(clock_1_out));
endmodule

module _3_register (
  input  Subtractor,
  input  [3:0] A,
  input  [3:0] B,
  input  ENABLE,
  output [3:0] REGISTER_OUT_A,
  output [3:0] REGISTER_OUT_B,
  output [3:0] OUTPUT,
  output CARRY
);

  wire clock_1_out;
  wire [3:0] Adder_s;

  Clock clock_1 (.out(clock_1_out));
  _4_bit_register Register (.in_2(clock_1_out), .in_3(ENABLE), .in_1(A), .out_4(REGISTER_OUT_A));
  _4_bit_register Register_2 (.in_2(clock_1_out), .in_3(ENABLE), .in_1(B), .out_4(REGISTER_OUT_B));
  _4_bit_parallel_adder Adder (.A(REGISTER_OUT_A), .B(REGISTER_OUT_B), .C(CARRY), .in_3(Subtractor), .S(Adder_s));
  _4_bit_register Register_3 (.in_2(clock_1_out), .in_3(ENABLE), .in_1(Adder_s), .out_4(OUTPUT));
endmodule

module _4_bit_parallel_adder (
  input  [3:0] A,
  input  [3:0] B,
  input  in_3,
  output [3:0] S,
  output C
);

  wire full_adder_1_c, full_adder_2_c, full_adder_3_c, full_adder_4_c, xor_2_out_3, xor_3_out_3, xor_4_out_3,
       xor_5_out_3;

  \xor  xor_1 (.in_1(in_3), .in_2(full_adder_1_c), .out_3(C));
  \xor  xor_2 (.in_1(in_3), .in_2(B[3]), .out_3(xor_2_out_3));
  Full_adder full_adder_1 (.C(full_adder_1_c), .A(xor_2_out_3), .B(A[3]), .S(S[3]), .C0(full_adder_2_c));
  \xor  xor_3 (.in_1(in_3), .in_2(B[1]), .out_3(xor_3_out_3));
  \xor  xor_4 (.in_1(in_3), .in_2(B[2]), .out_3(xor_4_out_3));
  Full_adder full_adder_2 (.C(full_adder_2_c), .A(xor_4_out_3), .B(A[2]), .S(S[2]), .C0(full_adder_3_c));
  \xor  xor_5 (.in_1(in_3), .in_2(B[0]), .out_3(xor_5_out_3));
  Full_adder full_adder_3 (.C(full_adder_3_c), .A(xor_3_out_3), .B(A[1]), .S(S[1]), .C0(full_adder_4_c));
  Full_adder full_adder_4 (.C(full_adder_4_c), .A(xor_5_out_3), .B(A[0]), .S(S[0]), .C0(in_3));
endmodule

module Full_adder (
  input  A,
  input  B,
  input  C0,
  output C,
  output S
);

  wire half_adder_1_c, half_adder_1_s, half_adder_2_c, nand_2_out, nand_3_out;

  nand nand_1 (C, nand_2_out, nand_3_out);
  nand nand_2 (nand_2_out, half_adder_1_c, half_adder_1_c);
  nand nand_3 (nand_3_out, half_adder_2_c, half_adder_2_c);
  Half_adder half_adder_1 (.A(A), .B(B), .S(half_adder_1_s), .C(half_adder_1_c));
  Half_adder half_adder_2 (.A(half_adder_1_s), .B(C0), .S(S), .C(half_adder_2_c));
endmodule

module Half_adder (
  input  A,
  input  B,
  output S,
  output C
);

  wire nand_1_out, nand_2_out, nand_3_out;

  nand nand_1 (nand_1_out, A, nand_2_out);
  nand nand_2 (nand_2_out, A, B);
  nand nand_3 (nand_3_out, nand_2_out, B);
  nand nand_4 (C, nand_2_out, nand_2_out);
  nand nand_5 (S, nand_1_out, nand_3_out);
endmodule

module _4_bit_register (
  input  [3:0] in_1,
  input  in_2,
  input  in_3,
  output [3:0] out_4
);

  D_flipflop d_flipflop_1 (.in_2(in_1[3]), .out_4(out_4[3]), .in_3(in_3), .in_1(in_2));
  D_flipflop d_flipflop_2 (.in_2(in_1[2]), .out_4(out_4[2]), .in_3(in_3), .in_1(in_2));
  D_flipflop d_flipflop_3 (.in_2(in_1[1]), .out_4(out_4[1]), .in_3(in_3), .in_1(in_2));
  D_flipflop d_flipflop_4 (.in_2(in_1[0]), .out_4(out_4[0]), .in_3(in_3), .in_1(in_2));
endmodule

module D_flipflop (
  input  in_1,
  input  in_2,
  input  in_3,
  output out_4
);

  wire and_1_out_3, and_2_out_3, nand_1_out, nand_2_out, nand_3_out, nand_4_out, nand_5_out, nand_6_out,
       nand_7_out;

  nand nand_1 (nand_1_out, in_1, in_1);
  nand nand_2 (nand_2_out, nand_1_out, nand_1_out);
  And and_1 (.in_1(in_1), .in_2(nand_3_out), .out_3(and_1_out_3));
  nand nand_3 (nand_3_out, nand_2_out, nand_2_out);
  And and_2 (.in_1(and_1_out_3), .in_2(in_3), .out_3(and_2_out_3));
  nand nand_4 (nand_4_out, in_2, in_2);
  nand nand_5 (nand_5_out, nand_4_out, and_2_out_3);
  nand nand_6 (nand_6_out, and_2_out_3, in_2);
  nand nand_7 (nand_7_out, nand_5_out, out_4);
  nand nand_8 (out_4, nand_7_out, nand_6_out);
endmodule

module \xor  (
  input  in_1,
  input  in_2,
  output out_3
);

  wire nand_1_out, nand_2_out, nand_3_out;

  nand nand_1 (nand_1_out, in_1, nand_2_out);
  nand nand_2 (nand_2_out, in_1, in_2);
  nand nand_3 (nand_3_out, nand_2_out, in_2);
  nand nand_4 (out_3, nand_1_out, nand_3_out);
endmodule

module And (
  input  in_1,
  input  in_2,
  output out_3
);

  wire nand_2_out;

  nand nand_1 (out_3, nand_2_out, nand_2_out);
  nand nand_2 (nand_2_out, in_1, in_2);
endmodule
