// Logisim project NAND.circ as structural Verilog: 1 circuit, main circuit main
module main (
  input  A,
  input  B,
  input  C,
  input  D,
  output A_prime_B_prime_C_prime_D_prime_AC
);

  wire A_prime_out, B_prime_out, C_prime_out, D_prime_out, nand_1_out, nand_2_out, nand_3_out, nand_4_out,
       nand_5_out, nand_6_out, nand_7_out, nand_8_out, nand_9_out, nand_10_out, nand_11_out;

  nand A_prime (A_prime_out, A, A);
  nand B_prime (B_prime_out, B, B);
  nand C_prime (C_prime_out, C, C);
  nand D_prime (D_prime_out, D, D);
  nand nand_1 (nand_1_out, A_prime_out, B_prime_out);
  nand nand_2 (nand_2_out, C_prime_out, D_prime_out);
  nand nand_3 (nand_3_out, A, C);
  nand nand_4 (nand_4_out, nand_1_out, nand_1_out);
  nand nand_5 (nand_5_out, nand_2_out, nand_2_out);
  nand nand_6 (nand_6_out, nand_3_out, nand_3_out);
  nand nand_7 (nand_7_out, nand_4_out, nand_4_out);
  nand nand_8 (nand_8_out, nand_5_out, nand_5_out);
  nand nand_9 (nand_9_out, nand_6_out, nand_6_out);
  nand nand_10 (nand_10_out, nand_7_out, nand_8_out);
  nand nand_11 (nand_11_out, nand_10_out, nand_10_out);
  nand nand_12 (A_prime_B_prime_C_prime_D_prime_AC, nand_11_out, nand_9_out);

  // Notes on the sheet:
  //   A'B'
  //   C'D'
  //   AC
  //   A'B'+C'D'
endmodule
